# Fritzing sketch rc-car-self-routed-pcb (saved by Fritzing 0.9.9b)
circuit board: 7.32837cm x 4.67548cm
breadboards: 1

parts:
  Steer_In = IC, SIP package, 3 pins [chip_label=IC]
  Acc_In = IC, SIP package, 3 pins [chip_label=IC]
  microSD1 = MicroSD Card Module
  Steer_Out = IC, SIP package, 3 pins [chip_label=IC]
  Acc_Out = IC, SIP package, 3 pins [chip_label=IC]
  A = USB Connectors [package=usb-a-s]
  MPU_6050 = InvenSense MPU6050
  Computing_Unit = Arduino Nano (Rev3.0) (ICSP)

nets:
  N1: Steer_In.pin1, Computing_Unit.D2
  VCC: Steer_In.pin2, Acc_In.pin2, microSD1.VCC, Steer_Out.pin2, Acc_Out.pin2, A.VBUS, MPU_6050.VCC, Computing_Unit.5V
  GND: Steer_In.pin3, Acc_In.pin3, microSD1.GND, Steer_Out.pin3, Acc_Out.pin3, A.GND, MPU_6050.GND, Computing_Unit.GND
  N2: Acc_In.pin1, Computing_Unit.D3
  N3: microSD1.MISO, Computing_Unit.D12/MISO
  N4: microSD1.MOSI, Computing_Unit.D11/MOSI
  N5: microSD1.SCK, Computing_Unit.D13/SCK
  N6: microSD1.CS, Computing_Unit.D4
  N7: Steer_Out.pin1, Computing_Unit.D9
  N8: Acc_Out.pin1, Computing_Unit.D10
  N9: A.D+, Computing_Unit.D0/RX
  N10: A.D-, Computing_Unit.D1/TX
  N11: MPU_6050.SCL, Computing_Unit.A5
  N12: MPU_6050.SDA, Computing_Unit.A4
