# Fritzing sketch rc-car (saved by Fritzing 0.9.9b)
circuit board: 7.32837cm x 4.67548cm
breadboards: 1

parts:
  Computing_Unit = Arduino Nano (Rev3.0) (ICSP)
  Steer_In = IC, SIP package, 3 pins [chip_label=IC]
  Acc_In = IC, SIP package, 3 pins [chip_label=IC]
  microSD1 = MicroSD Card Module
  Steer_Out = IC, SIP package, 3 pins [chip_label=IC]
  Acc_Out = IC, SIP package, 3 pins [chip_label=IC]
  A = USB Connectors [package=usb-a-s]
  Bauteil1 = InvenSense MPU6050

nets:
  N1: Computing_Unit.D1/TX, A.D-
  N2: Computing_Unit.D0/RX, A.D+
  GND: Computing_Unit.GND, Steer_In.pin3, Acc_In.pin3, microSD1.GND, Steer_Out.pin3, Acc_Out.pin3, A.GND, Bauteil1.GND
  N3: Computing_Unit.D2, Steer_In.pin1
  N4: Computing_Unit.D3, Acc_In.pin1
  N5: Computing_Unit.D4, Computing_Unit.D10, microSD1.CS, Acc_Out.pin1
  N6: Computing_Unit.D9, Steer_Out.pin1
  N7: Computing_Unit.D11/MOSI, microSD1.MOSI
  VCC: Computing_Unit.5V, Steer_In.pin2, Acc_In.pin2, microSD1.VCC, Steer_Out.pin2, Acc_Out.pin2, A.VBUS, Bauteil1.VCC
  N8: Computing_Unit.A5, Bauteil1.SCL
  N9: Computing_Unit.A4, Bauteil1.SDA
  N10: Computing_Unit.D13/SCK, microSD1.SCK
  N11: Computing_Unit.D12/MISO, microSD1.MISO
